# Fritzing sketch toy-alarm_new (saved by Fritzing 0.9.3b)
breadboards: 1

parts:
  Part1 = Adafruit Audio FX Mini Sound Board [part_number="Adafruit #2342 and #2220"]
  Part2 = Mono 2.5W Class D Audio Amplifier - PAM8302
  U1 = attiny85 [package=dip]
  R1 = Resistor [tolerance=±5% resistance=220 package="1206 [SMD]"]
  R3 = Resistor [tolerance=±5% resistance=220 package="1206 [SMD]"]  # not connected
  LED1 = LED - 5mm [color="White (8000K)" package="5 mm [THT]"]  # not connected
  LED2 = LED - 5mm [color="White (8000K)" package="5 mm [THT]"]  # not connected
  LED3 = LED - 5mm [color="White (8000K)" package="5 mm [THT]"]  # not connected
  S2 = SWITCH-DPDT [package=os]
  Part3 = Adafruit Pro Trinket LiIon/LiPoly Backpack [part_number="Adafruit #2124"]
  Part5 = PowerBoost 1000 Basic
  C1 = Electrolytic Capacitor [capacitance=47µF package="100 mil [THT, electrolytic]"]
  Q1 = Basic FET N-Channel [package="D2Pak [SMD]"]
  U2 = LIPO-1000mAh [package=lipo-1000]  # not connected
  JP1 = Header 6 [package=1x06-smd_edge]
  R2 = Resistor [tolerance=±5% resistance=220 package="1206 [SMD]"]

nets (from the breadboard view):
  GND: Part1.GND, Part2.GND, Part2.AIN-, U1.Pin_4, Part3.GND, Part5.GND, C1.-, JP1.1
  N1: Part1.GPIO0_2, U1.Pin_3
  N2: Part1.GPIO0_1, U1.Pin_6
  VIN: Part1.VIN, Part2.VCC, Q1.drain
  N3: Part1.VBUS, S2.5
  N4: Part1.L_AC, Part2.AIN+
  N5: U1.Pin_2, R1.Pin_1
  N6: U1.Pin_5, JP1.5
  N7: U1.Pin_7, JP1.6
  N8: U1.Pin_8, Part5.5.0V, C1.+, Q1.source, JP1.2, R2.Pin_0
  N9: R1.Pin_0, Q1.Gate, R2.Pin_1
  N10: S2.1, Part5.VBAT
  N11: S2.2, Part3.VBAT
  N12: S2.4, Part3.VBUS

notes:
  Simple RF M4 Receiver - 315MHz Momentary
  Boost converter (3v->5v) output
  DPDT chooses between charging and "on"
  This side is powered up only when needed (controled by the FET)

custom parts:
  Adafruit Audio FX Mini Sound Board: Would you like to add audio/sound effects to your next project, without an Arduino+Shield? Or maybe you don't even know how to use microcontrollers, you just want to make a sound play whenever you press a button. What about something that has to be very small and portable? You are probably feeling a little frustrated: it's been very hard to find a simple, low cost audio effects trigger that is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
  Mono 2.5W Class D Audio Amplifier - PAM8302: A super small but powerful mono amplifier able to deliver up to 2.5 Watts into 4-8 ohm impedance speakers. Inside the miniature chip is a class D controller, able to run from 2.0V-5.5VDC. Since the amp is a class D, its very efficient (over 90% efficient when driving an 8Ω speaker at over half a Watt) - making it perfect for portable and battery-powered projects.
  Adafruit Pro Trinket LiIon/LiPoly Backpack: If you have a Pro Trinket you probably know it's the perfect little size for a portable project. This LiPoly backpack makes it really easy to do! Instead of wiring 2 or 3 boards together to make a charging system, this little PCB sits on top of the Pro Trinket and allows a LiPoly/LiIon battery to plug in. When the Pro Trinket USB port is powered, the battery is recharged automatically. Unplug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
  PowerBoost 1000 Basic: The PowerBoost 1000 is a little DC/DC boost converter module that can run from 1.8V batteries or higher, and convert the battery output to 5.2V DC for running your 5V projects. At its heart is a TPS61030 boost converter from TI. This boost converter chip has some really nice extras such as low battery detection, 4A internal switch, synchronous conversion, excellent efficiency, and 700KHz high-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
